# Fritzing sketch backpack_circuit (saved by Fritzing 0.9.2b)
breadboards: 1

parts:
  Bauteil1 = Arduino Uno (Rev3)
  Bauteil2 = Triple Axis Accelerometer Breakout - ADXL335
  R1 = Temperature Sensor (Thermistor) [thermistor_type=NTC package=THT]
  R2 = Resistor [tolerance=±5% resistance=10k package="2010 [SMD]"]
  R3 = PHOTOCELL [package=photocell]
  R4 = Resistor [tolerance=±5% resistance=220 package="2010 [SMD]"]

nets:
  N1: Bauteil1.A0, R3.P$2, R4.Pin_0
  N2: Bauteil1.A2, R1.pin_1, R2.Pin_0
  N3: Bauteil1.A3, Bauteil2.ZOUT
  N4: Bauteil1.A4/SDA, Bauteil2.YOUT
  N5: Bauteil1.A5/SCL, Bauteil2.XOUT
  5V: Bauteil1.5V, Bauteil2.VCC, R2.Pin_1, R4.Pin_1
  GND: Bauteil1.GND, Bauteil2.GND, R1.pin_0, R3.P$1
